// Logisim project datapath.circ as structural Verilog: 1 circuit, main circuit main
module main (
);

  wire and_1_out, and_2_out, and_3_out, and_4_out, and_5_out, and_6_out, and_7_out, and_8_out, and_9_out,
       and_10_out, and_11_out, and_12_out, and_13_out, and_14_out, and_15_out, and_16_out, bit0, bit1, bit2,
       bit3, chkZ, CLK, Dec_out0, Dec_out1, Dec_out2, Dec_out3, Dec_out4, Dec_out5, Dec_out6, Dec_out7,
       Dec_out8, Dec_out9, Dec_out10, Dec_out11, Dec_out12, Dec_out13, Dec_out14, Dec_out15, DrALU, DrMEM,
       DrOFF, DrPC, DrREG, LdA, LdB, LdIR, LdMAR, LdPC, LdZ, nor_1_out, not_1_out, OPTest, WrMEM, WrREG,
       Z_out;
  wire [1:0] func;
  wire [2:0] Opcode;
  wire [3:0] regno, RX, RY;
  wire [4:4] IR_q;
  wire [5:0] multiplexer_3_out, Sequencer_ROM_data, State_Register_q, Z_ROM_data;
  wire [15:0] A_min_B, A_NAND_B, A_out, A_plus_1, A_plus_B, B_out, controlled_buffer_1_out, Memory_dout,
       multiplexer_1_out, multiplexer_5_out, multiplexer_6_out, PC_q, R0_always0, R0_out, R1_out, R2_out,
       R3_out, R4_out, R5_out, R6_out, R7_out, R8_out, R9_out, R10_out, R11_out, R12_out, R13_out, R14_out,
       R15_out, register_1_q;
  wire [20:0] Main_ROM_data;

  Clock clock_1 (.out(CLK));
  Register #(.width(16)) PC (.D(controlled_buffer_1_out), .en(LdPC), .clk(CLK), .Q(PC_q));  // open: clr
  assign controlled_buffer_1_out = DrPC ? PC_q : 16'bz;  // Controlled_Buffer controlled_buffer_1
  Adder #(.width(16)) adder_1 (.a(A_out), .b(B_out), .out(A_plus_B));  // open: cin, cout
  nor nor_1 (nor_1_out, controlled_buffer_1_out[15], controlled_buffer_1_out[14], controlled_buffer_1_out[13], controlled_buffer_1_out[12], controlled_buffer_1_out[11], controlled_buffer_1_out[10], controlled_buffer_1_out[9], controlled_buffer_1_out[8], controlled_buffer_1_out[7], controlled_buffer_1_out[6], controlled_buffer_1_out[5], controlled_buffer_1_out[4], controlled_buffer_1_out[3], controlled_buffer_1_out[2], controlled_buffer_1_out[1], controlled_buffer_1_out[0]);
  Register #(.width(1)) Z (.D(nor_1_out), .en(LdZ), .clk(CLK), .Q(Z_out));  // open: clr
  Register #(.width(16)) A (.D(controlled_buffer_1_out), .en(LdA), .clk(CLK), .Q(A_out));  // open: clr
  Subtractor #(.width(16)) subtractor_1 (.a(A_out), .b(B_out), .out(A_min_B));  // open: bin, bout
  Multiplexer #(.select(2), .width(16)) multiplexer_1 (
    .in0(A_plus_B), .in1(A_NAND_B), .in2(A_min_B), .in3(A_plus_1), .out(multiplexer_1_out), .sel(func));
  // Probe on multiplexer_1_out
  assign controlled_buffer_1_out = DrALU ? multiplexer_1_out : 16'bz;  // Controlled_Buffer controlled_buffer_2
  // Probe on controlled_buffer_1_out
  Register #(.width(16)) B (.D(controlled_buffer_1_out), .en(LdB), .clk(CLK), .Q(B_out));  // open: clr
  assign A_NAND_B = ~(A_out & B_out);  // NAND_Gate nand_1, 16 bits wide
  Register #(.width(6)) State_Register (
    .D(multiplexer_3_out), .en(1'b1), .clk(CLK), .Q(State_Register_q));  // open: clr
  Adder #(.width(16)) adder_2 (.a(A_out), .b(16'h1), .out(A_plus_1));  // open: cin, cout
  ROM #(.addrWidth(6), .dataWidth(25)) Main_ROM (
    .addr(State_Register_q),
    .data({chkZ, OPTest, func, Main_ROM_data[20:19], WrMEM, WrREG, LdZ, LdB, LdA, LdMAR, LdIR, LdPC, DrOFF, DrPC, DrALU, DrMEM, DrREG, Main_ROM_data[5:0]}));
  Multiplexer #(.width(16)) multiplexer_2 (.in0(R0_out), .in1({16{1'b0}}), .out(R0_always0), .sel(1'b1));
  Multiplexer #(.select(2), .width(6)) multiplexer_3 (
    .in0(Main_ROM_data[5:0]), .in1(Sequencer_ROM_data), .in2(Z_ROM_data), .out(multiplexer_3_out),
    .sel({chkZ, OPTest}));  // open: in3
  Register #(.width(16)) R0 (.D(controlled_buffer_1_out), .en(and_1_out), .clk(CLK), .Q(R0_out));  // open: clr
  and and_1 (and_1_out, Dec_out0, WrREG);
  Register #(.width(16)) R4 (.D(controlled_buffer_1_out), .en(and_2_out), .clk(CLK), .Q(R4_out));  // open: clr
  and and_2 (and_2_out, Dec_out4, WrREG);
  Register #(.width(16)) R8 (.D(controlled_buffer_1_out), .en(and_3_out), .clk(CLK), .Q(R8_out));  // open: clr
  and and_3 (and_3_out, Dec_out8, WrREG);
  Register #(.width(16)) R12 (.D(controlled_buffer_1_out), .en(and_4_out), .clk(CLK), .Q(R12_out));  // open: clr
  and and_4 (and_4_out, Dec_out12, WrREG);
  Multiplexer #(.select(2), .width(4)) multiplexer_4 (
    .in0(RX), .in1(RY), .in2({bit3, bit2, bit1, bit0}), .out(regno), .sel(Main_ROM_data[20:19]));  // open: in3
  ROM #(.addrWidth(3), .dataWidth(6)) Sequencer_ROM (.addr(Opcode), .data(Sequencer_ROM_data));
  ROM #(.addrWidth(2), .dataWidth(6)) Z_ROM (.addr({1'b0, Z_out}), .data(Z_ROM_data));
  and and_5 (and_5_out, Dec_out1, WrREG);
  and and_6 (and_6_out, Dec_out5, WrREG);
  and and_7 (and_7_out, Dec_out9, WrREG);
  and and_8 (and_8_out, Dec_out13, WrREG);
  Decoder #(.select(4)) decoder_1 (
    .out0(Dec_out0), .out1(Dec_out1), .out2(Dec_out2), .out3(Dec_out3), .out4(Dec_out4), .out5(Dec_out5),
    .out6(Dec_out6), .out7(Dec_out7), .out8(Dec_out8), .out9(Dec_out9), .out10(Dec_out10), .out11(Dec_out11),
    .out12(Dec_out12), .out13(Dec_out13), .out14(Dec_out14), .out15(Dec_out15), .sel(regno));  // open: en
  Register #(.width(16)) R1 (.D(controlled_buffer_1_out), .en(and_5_out), .clk(CLK), .Q(R1_out));  // open: clr
  Register #(.width(16)) R5 (.D(controlled_buffer_1_out), .en(and_6_out), .clk(CLK), .Q(R5_out));  // open: clr
  Register #(.width(16)) R9 (.D(controlled_buffer_1_out), .en(and_7_out), .clk(CLK), .Q(R9_out));  // open: clr
  Register #(.width(16)) R13 (.D(controlled_buffer_1_out), .en(and_8_out), .clk(CLK), .Q(R13_out));  // open: clr
  and and_9 (and_9_out, Dec_out2, WrREG);
  and and_10 (and_10_out, Dec_out6, WrREG);
  and and_11 (and_11_out, Dec_out10, WrREG);
  and and_12 (and_12_out, Dec_out14, WrREG);
  Register #(.width(16)) R2 (.D(controlled_buffer_1_out), .en(and_9_out), .clk(CLK), .Q(R2_out));  // open: clr
  Register #(.width(16)) R6 (.D(controlled_buffer_1_out), .en(and_10_out), .clk(CLK), .Q(R6_out));  // open: clr
  Register #(.width(16)) R10 (.D(controlled_buffer_1_out), .en(and_11_out), .clk(CLK), .Q(R10_out));  // open: clr
  Register #(.width(16)) R14 (.D(controlled_buffer_1_out), .en(and_12_out), .clk(CLK), .Q(R14_out));  // open: clr
  Multiplexer #(.select(4), .width(16)) multiplexer_5 (
    .in0(R0_always0), .in1(R1_out), .in2(R2_out), .in3(R3_out), .in4(R4_out), .in5(R5_out), .in6(R6_out),
    .in7(R7_out), .in8(R8_out), .in9(R9_out), .in10(R10_out), .in11(R11_out), .in12(R12_out), .in13(R13_out),
    .in14(R14_out), .in15(R15_out), .out(multiplexer_5_out), .sel(regno));
  assign controlled_buffer_1_out = DrREG ? multiplexer_5_out : 16'bz;  // Controlled_Buffer controlled_buffer_3
  // Probe on controlled_buffer_1_out
  and and_13 (and_13_out, Dec_out3, WrREG);
  and and_14 (and_14_out, Dec_out7, WrREG);
  and and_15 (and_15_out, Dec_out11, WrREG);
  and and_16 (and_16_out, Dec_out15, WrREG);
  Register #(.width(16)) R3 (.D(controlled_buffer_1_out), .en(and_13_out), .clk(CLK), .Q(R3_out));  // open: clr
  Register #(.width(16)) R7 (.D(controlled_buffer_1_out), .en(and_14_out), .clk(CLK), .Q(R7_out));  // open: clr
  Register #(.width(16)) R11 (.D(controlled_buffer_1_out), .en(and_15_out), .clk(CLK), .Q(R11_out));  // open: clr
  Register #(.width(16)) R15 (.D(controlled_buffer_1_out), .en(and_16_out), .clk(CLK), .Q(R15_out));  // open: clr
  Register #(.width(16)) register_1 (
    .D(controlled_buffer_1_out), .en(LdMAR), .clk(CLK), .Q(register_1_q));  // open: clr
  RAM #(.addrWidth(16), .dataWidth(16), .trigger("high")) Memory (
    .addr(register_1_q), .we(WrMEM), .oe(not_1_out), .din(controlled_buffer_1_out), .dout(Memory_dout));
  not not_1 (not_1_out, WrMEM);
  // Probe on Memory_dout
  assign controlled_buffer_1_out = DrMEM ? Memory_dout : 16'bz;  // Controlled_Buffer controlled_buffer_4
  // Probe on {{12{1'b0}}, bit3, bit2, bit1, bit0}
  // Probe on {{12{1'b1}}, bit3, bit2, bit1, bit0}
  Register #(.width(16)) IR (
    .D(controlled_buffer_1_out), .en(LdIR), .clk(CLK), .Q({Opcode, RX, RY, IR_q[4], bit3, bit2, bit1, bit0}));  // open: clr
  assign controlled_buffer_1_out = DrOFF ? multiplexer_6_out : 16'bz;  // Controlled_Buffer controlled_buffer_5
  Multiplexer #(.width(16)) multiplexer_6 (
    .in0({{12{1'b0}}, bit3, bit2, bit1, bit0}), .in1({{12{1'b1}}, bit3, bit2, bit1, bit0}),
    .out(multiplexer_6_out), .sel(IR_q[4]));
  // Probe on multiplexer_6_out

  // Other names for the same wires on the sheet: RZ[3:0] = {bit3, bit2, bit1, bit0}

  // Notes on the sheet:
  //   contents of Main_ROM (hex, n*v repeats v):
  //   6201 1082 e00900 104044 88045 20100 104047 88048 220100 440a 8804b 20100 440d 8804e 210f 20080 4411
  //   88052 2113 40040 4055 88056 410117 1000000 4219 8400 900 a021c 840 1d
  //   contents of Sequencer_ROM (hex, n*v repeats v):
  //   3 6 9 c 10 14 1b 1d
  //   contents of Z_ROM (hex, n*v repeats v):
  //   0 18
endmodule
